# Fritzing sketch circuit (saved by Fritzing 0.9.3b)
breadboards: 1

parts:
  Part1 = Arduino Nano (Rev3.0)
  IC1 = Voltage Regulator [package=to-220-alt]
  Grove1 = Grove OLED 128x96
  U1 = MLX90614 [package=to-39]
  C1 = Tantalum Capacitor [capacitance=0.1µF package="D 7343 [SMD, tantalum]"]
  C2 = Tantalum Capacitor [capacitance="1 μF" package="C 6032 [SMD, tantalum]"]
  IC2 = IC, DIP package, 8 pins [chip_label=ADM485]
  LED1 = LED - 5mm [color="Red (633nm)" package="5 mm [THT]"]
  R1 = Resistor [tolerance=±5% resistance=220 package=THT]
  R2 = Resistor [tolerance=±5% resistance=3.3k package=THT]
  R3 = Resistor [tolerance=±5% resistance=3.3k package=THT]

nets (from the schematic view):
  N1: Part1.D1/TX, IC2.pin1
  N2: Part1.D0/RX, IC2.pin4
  GND: Part1.GND, IC1.GND, Grove1.GND, U1.VSS, C1.-, C2.-, IC2.pin5, R1.Pin_1
  N3: Part1.D2, IC2.pin2, IC2.pin3, LED1.cathode
  N4: Part1.5V, IC1.OUT, C2.+, IC2.pin8
  N5: Part1.A5, Grove1.SDA, U1.SCL_VZ, R2.Pin_0
  N6: Part1.A4, Grove1.SCL, U1.PWM_SDA, R3.Pin_0
  3.3V: Part1.3V3, Grove1.VCC, U1.VDD, C1.+, R2.Pin_1, R3.Pin_1
  12V: IC1.IN

notes:
  B
  A
